# Fritzing sketch ESquematicoAraña (saved by Fritzing 0.8.7b)

parts:
  J1 = Basic Servo
  J2 = Basic Servo
  J3 = Basic Servo
  J4 = Basic Servo
  J5 = Basic Servo
  J6 = Basic Servo
  BT1 = Bluetooth HC-06u [package=THT]
  BAT1 = BC9VPC [package=bc9vpc]
  J9 = Basic Servo
  Nano1 = Arduino Nano v2.3
  J8 = Basic Servo
  J11 = Basic Servo
  J12 = Basic Servo
  J10 = Basic Servo
  J7 = Basic Servo

nets:
  GND: J1.gnd, J2.gnd, J3.gnd, J4.gnd, J5.gnd, J6.gnd, BT1.GND, BAT1.V+, J9.gnd, Nano1.GND, J8.gnd, J11.gnd, J12.gnd, J10.gnd, J7.gnd
  VCC: J1.vcc, J2.vcc, J3.vcc, J4.vcc, J5.vcc, J6.vcc, BAT1.V-, J9.vcc, J8.vcc, J11.vcc, J12.vcc, J10.vcc, J7.vcc
  N1: J1.pulse, Nano1.D13
  N2: J2.pulse, Nano1.D12
  N3: J3.pulse, Nano1.D11
  N4: J4.pulse, Nano1.D10
  N5: J5.pulse, Nano1.D9
  N6: J6.pulse, Nano1.D8
  VCC_2: BT1.VCC, Nano1.+5V
  N7: BT1.TXD, Nano1.D0RX
  N8: BT1.RXD, Nano1.D1TX
  N9: J9.pulse, Nano1.D2
  N10: Nano1.D3, J8.pulse
  N11: Nano1.D4, J7.pulse
  N12: Nano1.D5, J12.pulse
  N13: Nano1.D6, J11.pulse
  N14: Nano1.D7, J10.pulse

custom parts:
  Bluetooth HC-06u: Bluetooth HC-06 - face up, pins down 16.5mm x 37.5mm PCB
