# Fritzing sketch EsquematicoBrazo (saved by Fritzing 0.9.3b)
breadboards: 1

parts:
  J3 = Basic Servo
  J5 = Basic Servo
  J4 = Basic Servo
  Componente1 = Arduino Mega 2560 (Rev3)
  BT1 = Bluetooth HC-06u
  J2 = Basic Servo
  VCC1 = 4 x AAA Battery Mount

nets:
  GND: J3.gnd, J5.gnd, J2.gnd, VCC1.-
  VCC: J3.vcc, J5.vcc, J2.vcc, VCC1.+
  N1: J3.pulse, Componente1.D9_PWM
  N2: J5.pulse, Componente1.D7_PWM
  N3: J4.pulse, Componente1.D8_PWM
  N4: Componente1.D10_PWM, J2.pulse
  N5: Componente1.5V, BT1.connector0
  N6: Componente1.D0_RX0, BT1.connector2
  N7: Componente1.D1_TX0, BT1.connector3
  N8: Componente1.GND, BT1.connector1
