# Fritzing sketch EsquematicoPropeller (saved by Fritzing 0.8.7b)

parts:
  Parte1 = Arduino Nano (Rev3.0)
  LED1 = LED - 5mm [color="Red (633nm)" package="5 mm [THT]"]
  LED2 = LED - 5mm [color="Red (633nm)" package="5 mm [THT]"]
  LED3 = LED - 5mm [color="Red (633nm)" package="5 mm [THT]"]
  LED4 = LED - 5mm [color="Red (633nm)" package="5 mm [THT]"]
  LED5 = LED - 5mm [color="Red (633nm)" package="5 mm [THT]"]
  LED6 = LED - 5mm [color="Red (633nm)" package="5 mm [THT]"]
  LED7 = LED - 5mm [color="Red (633nm)" package="5 mm [THT]"]
  LED8 = LED - 5mm [color="Red (633nm)" package="5 mm [THT]"]
  LED9 = LED - 5mm [color="Red (633nm)" package="5 mm [THT]"]
  LED10 = LED - 5mm [color="Red (633nm)" package="5 mm [THT]"]
  LED11 = LED - 5mm [color="Red (633nm)" package="5 mm [THT]"]
  LED12 = LED - 5mm [color="Red (633nm)" package="5 mm [THT]"]
  LED13 = LED - 5mm [color="Red (633nm)" package="5 mm [THT]"]
  LED14 = LED - 5mm [color="Red (633nm)" package="5 mm [THT]"]
  LED16 = LED - 5mm [color="Red (633nm)" package="5 mm [THT]"]
  LED17 = LED - 5mm [color="Red (633nm)" package="5 mm [THT]"]
  Q1 = PNP-Transistor [package="SOT-23 [SMD]"]
  R1 = Resistor [tolerance=±5% resistance=220 package="0603 [SMD]"]
  R2 = Resistor [tolerance=±5% resistance=220 package="0603 [SMD]"]
  R3 = Resistor [tolerance=±5% resistance=220 package="0603 [SMD]"]
  R4 = Resistor [tolerance=±5% resistance=220 package="0603 [SMD]"]
  R5 = Resistor [tolerance=±5% resistance=220 package="0603 [SMD]"]
  R6 = Resistor [tolerance=±5% resistance=220 package="0603 [SMD]"]
  R7 = Resistor [tolerance=±5% resistance=220 package="0603 [SMD]"]
  R8 = Resistor [tolerance=±5% resistance=220 package="0603 [SMD]"]
  R9 = Resistor [tolerance=±5% resistance=220 package="0603 [SMD]"]
  R10 = Resistor [tolerance=±5% resistance=220 package="0603 [SMD]"]
  R11 = Resistor [tolerance=±5% resistance=220 package="0603 [SMD]"]
  R12 = Resistor [tolerance=±5% resistance=220 package="0603 [SMD]"]
  R13 = Resistor [tolerance=±5% resistance=220 package="0603 [SMD]"]
  R14 = Resistor [tolerance=±5% resistance=220 package="0603 [SMD]"]
  R15 = Resistor [tolerance=±5% resistance=220 package="0603 [SMD]"]
  R16 = Resistor [tolerance=±5% resistance=220 package="0603 [SMD]"]
  U1 = LIPO-110mAh [package=lipo-110]
  R17 = Resistor [tolerance=±5% resistance=220 package="0603 [SMD]"]

nets:
  N1: Parte1.GND, LED1.cathode, LED2.cathode, LED3.cathode, LED4.cathode, LED5.cathode, LED6.cathode, LED7.cathode, LED8.cathode, LED9.cathode, LED10.cathode, LED11.cathode, LED12.cathode, LED13.cathode, LED14.cathode, Q1.0, U1.-
  N2: Parte1.D2, R16.Pin_1
  N3: Parte1.D3, R13.Pin_1
  N4: Parte1.D4, R14.Pin_1
  N5: Parte1.D5, R15.Pin_1
  N6: Parte1.D6, R10.Pin_1
  N7: Parte1.D7, R11.Pin_1
  N8: Parte1.D8, R12.Pin_1
  N9: Parte1.D9, R7.Pin_1
  N10: Parte1.D10, R8.Pin_1
  N11: Parte1.D11/MOSI, R9.Pin_1
  N12: Parte1.D12/MISO, R4.Pin_1
  N13: Parte1.5V, Q1.2, U1.+, R17.Pin_1
  N14: Parte1.A5, R1.Pin_1
  N15: Parte1.A4, R2.Pin_1
  N16: Parte1.A3, R3.Pin_1
  N17: Parte1.A2, R6.Pin_1
  N18: Parte1.A1, R5.Pin_1
  N19: Parte1.A0, Q1.1, R17.Pin_0
  N20: LED1.anode, R7.Pin_0
  N21: LED2.anode, R12.Pin_0
  N22: LED3.anode, R11.Pin_0
  N23: LED4.anode, R10.Pin_0
  N24: LED5.anode, R13.Pin_0
  N25: LED6.anode, R15.Pin_0
  N26: LED7.anode, R16.Pin_0
  N27: LED8.anode, R14.Pin_0
  N28: LED9.anode, R9.Pin_0
  N29: LED10.anode, R5.Pin_0
  N30: LED11.anode, R8.Pin_0
  N31: LED12.anode, R4.Pin_0
  N32: LED13.anode, R3.Pin_0
  N33: LED14.anode, R6.Pin_0
  N34: LED16.cathode, LED17.cathode
  N35: LED16.anode, R2.Pin_0
  N36: LED17.anode, R1.Pin_0
