# Fritzing sketch EsquematicoWallE (saved by Fritzing 0.9.3b)

parts:
  Componente1 = Arduino Mega 2560 (Rev3)
  hc-sr1 = hc-sr04
  M1 = DC Motor
  S1 = H-Bridge with L298N
  M2 = DC Motor
  VCC1 = 4 x AAA Battery Mount

nets:
  GND: Componente1.GND, hc-sr1.GND
  5V: Componente1.5V, hc-sr1.VCC
  N1: Componente1.D2_PWM, hc-sr1.Trig
  N2: Componente1.D3_PWM, hc-sr1.Echo
  N3: Componente1.D4_PWM, S1.IN1
  N4: Componente1.D5_PWM, S1.IN2
  N5: Componente1.D6_PWM, S1.IN3
  N6: Componente1.D7_PWM, S1.IN4
  N7: M1.pin_1, S1.OUT1-Motor1
  N8: M1.pin_2, S1.OUT2-Motor1
  N9: S1.12V, VCC1.+
  N10: S1.GND, VCC1.-
  N11: S1.OUT3-Motor2, M2.pin_2
  N12: S1.OUT4-Motor2, M2.pin_1

custom parts:
  H-Bridge with L298N: h-bridge
